# Fritzing sketch led segments (saved by Fritzing 0.9.3b)
breadboards: 2

parts:
  Raspberry_Pi_1 = Raspberry Pi 3 [part_number=RPI-3-V1.2]
  DI1 = 7-Segment LED Display [package=THT]
  DI2 = 7-Segment LED Display [package=THT]
  IC1 = IC, DIP package, 16 pins [chip_label=IC]
  R4 = Resistor [tolerance=±5% resistance=220 package=THT]
  R7 = Resistor [tolerance=±5% resistance=220 package=THT]
  R8 = Resistor [tolerance=±5% resistance=220 package=THT]
  R9 = Resistor [tolerance=±5% resistance=220 package=THT]
  R10 = Resistor [tolerance=±5% resistance=220 package=THT]
  R11 = Resistor [tolerance=±5% resistance=220 package=THT]
  R12 = Resistor [tolerance=±5% resistance=220 package=THT]
  Q1 = NPN-Transistor [package="SOT-23 [SMD]"]
  Q2 = PNP-Transistor [package="SOT-23 [SMD]"]
  Q3 = NPN-Transistor [package="SOT-23 [SMD]"]
  Q4 = PNP-Transistor [package="SOT-23 [SMD]"]  # not connected
  Q5 = NPN-Transistor [package="SOT-23 [SMD]"]
  Q6 = PNP-Transistor [package="SOT-23 [SMD]"]
  Q7 = NPN-Transistor [package="SOT-23 [SMD]"]
  Q8 = PNP-Transistor [package="SOT-23 [SMD]"]
  Q9 = NPN-Transistor [package="SOT-23 [SMD]"]
  Q10 = PNP-Transistor [package="SOT-23 [SMD]"]
  Q11 = NPN-Transistor [package="SOT-23 [SMD]"]
  Q12 = PNP-Transistor [package="SOT-23 [SMD]"]
  DI3 = 7-Segment LED Display [package=THT]
  DI4 = 7-Segment LED Display [package=THT]
  DI5 = 7-Segment LED Display [package=THT]
  DI6 = 7-Segment LED Display [package=THT]

nets:
  N1: Raspberry_Pi_1.GPIO2, Q6.0
  N2: Raspberry_Pi_1.GPIO3, Q12.0
  N3: Raspberry_Pi_1.GIPO4, Q10.0
  N4: Raspberry_Pi_1.GIPO17, Q8.0
  N5: Raspberry_Pi_1.GIPO22, Q2.0
  N6: Raspberry_Pi_1.GIPO5, IC1.pin6
  N7: Raspberry_Pi_1.GIPO6, IC1.pin2
  N8: Raspberry_Pi_1.GIPO13, IC1.pin1
  N9: Raspberry_Pi_1.GIPO19, IC1.pin7
  N10: Raspberry_Pi_1.GND, IC1.pin8
  N11: DI1.cathodeE, R9.Pin_1
  N12: DI1.cathodeD, R8.Pin_1
  N13: DI1.cathodeC, DI2.cathodeC, R7.Pin_1
  N14: DI1.cathodeB, R4.Pin_1
  N15: DI1.cathodeA, R10.Pin_1
  N16: DI1.cathodeF, R11.Pin_1
  N17: DI1.cathodeG, R12.Pin_1
  N18: DI2.commAnode, Q3.2
  N19: IC1.pin3, IC1.pin5, Q1.1, Q2.2, Q3.1
  N20: IC1.pin9, R9.Pin_0
  N21: IC1.pin10, R8.Pin_0
  N22: IC1.pin11, R7.Pin_0
  N23: IC1.pin12, R4.Pin_0
  N24: IC1.pin13, R10.Pin_0
  N25: IC1.pin14, R12.Pin_0
  N26: IC1.pin15, R11.Pin_0
  N27: Q1.0, Q2.1
  N28: Q5.2, DI6.commAnode
  N29: Q5.0, Q6.1
  N30: Q5.1, Q6.2, Q7.1, Q8.2, Q9.1, Q10.2, Q11.1, Q12.2
  N31: Q7.2, DI3.commAnode
  N32: Q7.0, Q8.1
  N33: Q9.2, DI4.commAnode
  N34: Q9.0, Q10.1
  N35: Q11.2, DI5.commAnode
  N36: Q11.0, Q12.1
